// Logisim project CompArch_Designs.circ as structural Verilog: 5 circuits, main circuit memory cell
module memory_cell (
  input  Clock,
  input  WE,
  input  Din,
  input  OE,
  input  Reset,
  output Dout,
  output Stored_data
);

  wire and_1_out, and_2_out, not_1_out, or_1_out;

  not not_1 (not_1_out, WE);
  and and_1 (and_1_out, Stored_data, not_1_out);
  and and_2 (and_2_out, WE, Din);
  or or_1 (or_1_out, and_1_out, and_2_out);
  D_Flip_Flop d_ff_1 (.clk(Clock), .D(or_1_out), .Q(Stored_data), .reset(Reset));  // open: Qn, preset, en
  assign Dout = OE ? Stored_data : 1'bz;  // Controlled_Buffer controlled_buffer_1

  // Notes on the sheet:
  //   Group members
  //   wondmeneh Dereje ugr/22556/13
  //   Hermona Addisu ugr/22516/13
  //   Natnael Zemedkun ugr/22762/13
  //   Sifen tesfa ugr/22681/13
  //   Sifen Tariku ugr/23181/13
  //   memory cell 
endmodule

module Register (
  input  Clock,
  input  WE,
  input  [7:0] Din,
  input  OE,
  output [7:0] Dout,
  output [7:0] Stored_Data
);

  memory_cell _0 (
    .Clock(Clock), .WE(WE), .Din(Din[0]), .OE(OE), .Dout(Dout[0]), .Stored_data(Stored_Data[0]));  // open: Reset
  memory_cell _1 (
    .Clock(Clock), .WE(WE), .Din(Din[1]), .OE(OE), .Dout(Dout[1]), .Stored_data(Stored_Data[1]));  // open: Reset
  memory_cell _2 (
    .Clock(Clock), .WE(WE), .Din(Din[2]), .OE(OE), .Dout(Dout[2]), .Stored_data(Stored_Data[2]));  // open: Reset
  memory_cell _3 (
    .Clock(Clock), .WE(WE), .Din(Din[3]), .OE(OE), .Dout(Dout[3]), .Stored_data(Stored_Data[3]));  // open: Reset
  memory_cell _4 (
    .Clock(Clock), .WE(WE), .Din(Din[4]), .OE(OE), .Dout(Dout[4]), .Stored_data(Stored_Data[4]));  // open: Reset
  memory_cell _5 (
    .Clock(Clock), .WE(WE), .Din(Din[5]), .OE(OE), .Dout(Dout[5]), .Stored_data(Stored_Data[5]));  // open: Reset
  memory_cell _6 (
    .Clock(Clock), .WE(WE), .Din(Din[6]), .OE(OE), .Dout(Dout[6]), .Stored_data(Stored_Data[6]));  // open: Reset
  memory_cell _7 (
    .Clock(Clock), .WE(WE), .Din(Din[7]), .OE(OE), .Dout(Dout[7]), .Stored_data(Stored_Data[7]));  // open: Reset

  // Notes on the sheet:
  //   Group members
  //   wondmeneh Dereje ugr/22556/13
  //   Hermona Addisu ugr/22516/13
  //   Natnael Zemedkun ugr/22762/13
  //   Sifen tesfa ugr/22681/13
  //   Sifen Tariku ugr/23181/13
  //   Register (8 bits)
endmodule

module MAR (
  input  Clock,
  input  [3:0] Dout,
  input  WE,
  input  [3:0] Din,
  input  OE,
  output [3:0] Stored_data
);

  memory_cell _0 (
    .Clock(Clock), .WE(WE), .Din(Din[0]), .OE(OE), .Dout(Dout[0]), .Stored_data(Stored_data[0]));  // open: Reset
  memory_cell _1 (
    .Clock(Clock), .WE(WE), .Din(Din[1]), .OE(OE), .Dout(Dout[1]), .Stored_data(Stored_data[1]));  // open: Reset
  memory_cell _2 (
    .Clock(Clock), .WE(WE), .Din(Din[2]), .OE(OE), .Dout(Dout[2]), .Stored_data(Stored_data[2]));  // open: Reset
  memory_cell _3 (
    .Clock(Clock), .WE(WE), .Din(Din[3]), .OE(OE), .Dout(Dout[3]), .Stored_data(Stored_data[3]));  // open: Reset

  // Notes on the sheet:
  //   Group members
  //   wondmeneh Dereje ugr/22556/13
  //   Hermona Addisu ugr/22516/13
  //   Natnael Zemedkun ugr/22762/13
  //   Sifen tesfa ugr/22681/13
  //   Sifen Tariku ugr/23181/13
  //   MAR
endmodule

module ALU (
  input  [7:0] Reg_A,
  input  [7:0] Reg_B,
  input  OE,
  output [7:0] Dout,
  output [7:0] ALU_Result,
  output Cout
);

  Adder adder_1 (.a(Reg_A), .b(Reg_B), .out(ALU_Result), .cout(Cout));  // open: cin
  assign Dout = OE ? ALU_Result : 8'bz;  // Controlled_Buffer controlled_buffer_1

  // Notes on the sheet:
  //   Group members
  //   Sifen tesfa ugr/22681/13
  //   Sifen Tariku ugr/23181/13
  //   wondmeneh Dereje ugr/22556/13
  //   Hermona Addisu ugr/22516/13
  //   Natnael Zemedkun ugr/22762/13
endmodule

module main (
  input  [7:0] Testing_Data,
  input  WE,
  input  OE_Testing_data,
  input  OE,
  input  Internal_OE,
  input  WE_2,
  input  WE_3,
  input  OE_2,
  input  OE_3,
  input  WE_4,
  input  WE_5,
  input  OE_4,
  input  WE_6,
  input  OE_5,
  output [3:0] MAR_content,
  output [7:0] IR_Content,
  output [7:0] MBR_content,
  output [7:0] Reg_A_content,
  output [7:0] ALU_Result,
  output [7:0] out_20,
  output [7:0] Reg_B_content
);

  wire clock_1_out;
  wire [3:0] bitselector_1_out, undriven;
  wire [7:0] ALU_dout, Instruction_Reg_dout;

  Clock clock_1 (.out(clock_1_out));
  BitSelector #(.group(4)) bitselector_1 (.in(Instruction_Reg_dout), .out(bitselector_1_out), .sel(1'b0));
  Register Instruction_Reg (
    .Clock(clock_1_out), .WE(WE_3), .Din(ALU_dout), .OE(OE_3), .Dout(Instruction_Reg_dout),
    .Stored_Data(IR_Content));
  Register register_1 (.Clock(clock_1_out), .WE(WE_4), .Din(ALU_dout), .Stored_Data(Reg_A_content));  // open: OE, Dout
  ALU ALU (
    .Reg_A(Reg_A_content), .Reg_B(Reg_B_content), .OE(OE_4), .Dout(ALU_dout), .ALU_Result(ALU_Result));  // open: Cout
  Register register_2 (.Clock(clock_1_out), .WE(WE_6), .Din(ALU_dout), .Stored_Data(Reg_B_content));  // open: OE, Dout
  LED D7 (.in(ALU_dout[7]));
  LED D6 (.in(ALU_dout[6]));
  LED D5 (.in(ALU_dout[5]));
  assign ALU_dout = OE_Testing_data ? Testing_Data : 8'bz;  // Controlled_Buffer controlled_buffer_1
  LED D3 (.in(ALU_dout[3]));
  LED D2 (.in(ALU_dout[2]));
  LED D4 (.in(ALU_dout[4]));
  LED D0 (.in(ALU_dout[0]));
  LED D1 (.in(ALU_dout[1]));
  assign ALU_dout = Internal_OE ? MBR_content : 8'bz;  // Controlled_Buffer controlled_buffer_2
  MAR MAR (.Clock(clock_1_out), .WE(WE), .Din(bitselector_1_out), .OE(OE), .Dout(undriven), .Stored_data(MAR_content));
  Register MBR (.Clock(clock_1_out), .WE(WE_2), .Din(ALU_dout), .OE(OE_2), .Dout(ALU_dout), .Stored_Data(MBR_content));
  Register register_3 (
    .Clock(clock_1_out), .WE(WE_5), .Din(ALU_dout), .OE(OE_5), .Dout(ALU_dout), .Stored_Data(out_20));
  LED D7_2 (.in(ALU_dout[7]));
  LED D6_2 (.in(ALU_dout[6]));
  LED D5_2 (.in(ALU_dout[5]));
  LED D4_2 (.in(ALU_dout[4]));
  LED D1_2 (.in(ALU_dout[1]));
  LED D2_2 (.in(ALU_dout[2]));
  LED D3_2 (.in(ALU_dout[3]));
  LED D0_2 (.in(ALU_dout[0]));

  // Notes on the sheet:
  //   Group members
  //   Hermona Addisu ugr/22516/13
  //   Sifen tesfa ugr/22681/13
  //   Sifen Tariku ugr/23181/13
  //   wondmeneh Dereje ugr/22556/13
  //   Natnael Zemedkun ugr/22762/13
  //   Register A
  //   Register B
  //   Internal Address Bus(4bits)
  //   Internal Data Bus
  //   Output Register
  //   External Address
  //   External Data Bus
endmodule
